// Digital circuit control_unit_conditional.dig as structural Verilog
module control_unit_conditional (
  input  [31:0] iw,
  input  [3:0] NZCV,
  input  CLK,
  output RFW,
  output EXT,
  output ALUop,
  output ALU1src,
  output BR,
  output BL,
  output BX
);

  wire AL_eq, and_1_out, C, comparator_1_eq, main_decoder_1_p2, main_decoder_1_p7, N, or_1_out, V, Z;

  // main_decoder main_decoder_1: pin names not known; wires that end beside it: iw, main_decoder_1_p2, RFW, EXT, ALUop, ALU1src, main_decoder_1_p7, BL, BX
  Register #(.Bits(4)) register_1 (.D(NZCV), .C(CLK), .en(main_decoder_1_p2), .Q({V, C, Z, N}));
  Comparator AL (.a(iw[28]), .b(1'b0), .eq(AL_eq));  // open: gt, lt
  Comparator comparator_1 (.a(iw[28]), .b(1'b0), .eq(comparator_1_eq));  // open: gt, lt
  and and_1 (and_1_out, Z, comparator_1_eq);
  or or_1 (or_1_out, AL_eq, and_1_out);
  and and_2 (BR, main_decoder_1_p7, or_1_out);
  // Pins of 1 and 4 bits meet at iw[31:28]
  // Pins of 1 and 4 bits meet at 4'b1110
  // Pins of 1 and 4 bits meet at 4'b0000
endmodule
