// Digital circuit processor_ext_unit.dig as structural Verilog
module processor_ext_unit (
  input  [31:0] IW,
  input  [1:0] S,
  output [31:0] extended
);

  Multiplexer #(.Selector_Bits(2), .Bits(32)) multiplexer_1 (
    .sel(S), .in_0({{24{1'b0}}, IW[7:0]}), .in_1({{20{1'b0}}, IW[11:0]}),
    .in_2({{7{IW[23]}}, IW[22:0], 2'b00}), .in_3({32{1'b0}}), .out(extended));
endmodule
